// Logisim project POTEC_Lights_Out.circ as structural Verilog: 6 circuits, main circuit main
module main (
);

  wire A, a_t, B, b_t, C, c_t, CA, CB, CC, CD, CE, CF, CG, CH, CI, CJ, CK, CL, CM, CN, CO, CP, CQ, CR, CS,
       CT, CU, CW, CX, CY, CZ, D, d_t, E, e_t, F, f_t, G, g_t, H, h_t, I, i_t, J, j_t, K, k_t, L, l_t, M,
       m_t, N, n_t, O, o_t, P, p_t, Q, q_t, R, r_t, RANDOMIZE, RESET, S, s_t, T, t_t, U, u_t, W, w_t, WIN, X,
       x_t, Y, y_t, Z, z_t;

  // RGB_Video #(.width(256)) rgb_video_1: pin names not known; wires that end beside it: a_t, f_t, k_t, p_t, u_t, b_t, g_t, l_t, q_t, w_t, c_t, h_t, m_t, r_t, x_t, d_t, i_t, n_t, s_t, y_t, e_t, j_t, o_t, t_t, z_t
  Button button_1 (.out(A));
  Button button_2 (.out(B));
  Button button_3 (.out(F));
  Button button_4 (.out(G));
  Button button_5 (.out(K));
  Button button_6 (.out(L));
  Button button_7 (.out(P));
  Button button_8 (.out(Q));
  Button button_9 (.out(U));
  Button button_10 (.out(W));
  Button button_11 (.out(C));
  Button button_12 (.out(H));
  Button button_13 (.out(M));
  Button button_14 (.out(R));
  Button button_15 (.out(X));
  Button button_16 (.out(D));
  Button button_17 (.out(E));
  Button button_18 (.out(I));
  Button button_19 (.out(J));
  Button button_20 (.out(N));
  Button button_21 (.out(O));
  Button button_22 (.out(S));
  Button button_23 (.out(T));
  Button button_24 (.out(Y));
  Button button_25 (.out(Z));
  LED led_1 (.in(WIN));
  Button button_26 (.out(RANDOMIZE));
  Button button_27 (.out(RESET));
  LED led_2 ();  // open: in
  LED led_3 ();  // open: in
  LED led_4 ();  // open: in
  LED led_5 ();  // open: in
  LED led_6 ();  // open: in
  LED led_7 ();  // open: in
  LED led_8 ();  // open: in
  LED led_9 ();  // open: in
  LED led_10 ();  // open: in
  LED led_11 ();  // open: in
  LED led_12 ();  // open: in
  LED led_13 ();  // open: in
  LED led_14 ();  // open: in
  LED led_15 ();  // open: in
  LED led_16 ();  // open: in
  LED led_17 ();  // open: in
  LED led_18 ();  // open: in
  LED led_19 ();  // open: in
  LED led_20 ();  // open: in
  LED led_21 ();  // open: in
  LED led_22 ();  // open: in
  LED led_23 ();  // open: in
  LED led_24 ();  // open: in
  LED led_25 ();  // open: in
  LED led_26 ();  // open: in
  button_setup_threes button_setup_threes_1 (
    .pA(A), .pB(B), .pD(D), .pE(E), .pF(F), .pJ(J), .pP(P), .pT(T), .pU(U), .pW(W), .pY(Y), .pZ(Z), .cA(CA),
    .cE(CE), .cU(CU), .cZ(CZ), .rst(RESET), .random_generator(RANDOMIZE), .dA(a_t), .dE(e_t), .dU(u_t),
    .dZ(z_t));
  button_setup_fours button_setup_fours_1 (
    .pA(A), .pB(B), .pC(C), .pD(D), .pE(E), .pF(F), .pG(G), .pH(H), .pI(I), .pJ(J), .pK(K), .pL(L), .pN(N),
    .pO(O), .pP(P), .pQ(Q), .pR(R), .pS(S), .pT(T), .pU(U), .pW(W), .pX(X), .pY(Y), .pZ(Z), .cB(CB), .cF(CF),
    .cW(CW), .cJ(CJ), .cC(CC), .cK(CK), .cX(CX), .cO(CO), .cD(CD), .cP(CP), .cY(CY), .cT(CT), .rst(RESET),
    .random_generator(RANDOMIZE), .dB(b_t), .dF(f_t), .dW(w_t), .dJ(j_t), .dC(c_t), .dK(k_t), .dX(x_t),
    .dO(o_t), .dT(t_t), .dD(d_t), .dP(p_t), .dY(y_t));
  button_setup_fives button_setup_fives_1 (
    .pA(A), .pB(B), .pC(C), .pD(D), .pE(E), .pF(F), .pG(G), .pH(H), .pI(I), .pJ(J), .pK(K), .pL(L), .pN(N),
    .pO(O), .pP(P), .pQ(Q), .pR(R), .pS(S), .pT(T), .pU(U), .pW(W), .pX(X), .pY(Y), .pZ(Z), .pM(M), .cG(CG),
    .cI(CI), .cH(CH), .cN(CN), .cM(CM), .cL(CL), .cR(CR), .cQ(CQ), .cS(CS), .rst(RESET),
    .random_generizer(RANDOMIZE), .dI(i_t), .dG(g_t), .dH(h_t), .dN(n_t), .dM(m_t), .dL(l_t), .dQ(q_t),
    .dR(r_t), .dS(s_t));
  randomizer randomizer_1 (
    .random_gen(RANDOMIZE), .a(CA), .b(CB), .c(CC), .d(CD), .e(CE), .f(CF), .g(CG), .h(CH), .i(CI), .j(CJ),
    .k(CK), .l(CL), .m(CM), .n(CN), .o(CO), .p(CP), .q(CQ), .r(CR), .s(CS), .t(CT), .u(CU), .w(CW), .x(CX),
    .y(CY), .z(CZ));
  wincon wincon_1 (
    .pA(a_t), .pB(b_t), .pC(c_t), .pD(d_t), .pE(e_t), .pF(f_t), .pG(g_t), .pH(h_t), .pI(i_t), .pJ(j_t),
    .pK(k_t), .pL(l_t), .pN(n_t), .pO(o_t), .pP(p_t), .pQ(q_t), .pR(r_t), .pS(s_t), .pT(t_t), .pU(u_t),
    .pW(w_t), .pX(x_t), .pY(y_t), .pZ(z_t), .pM(m_t), .random(RANDOMIZE), .reset(RESET), .WIN(WIN));

  // Notes on the sheet:
  //   CEL GRY:
  //   Instrukcja gry:
  //   Wyłączyć wszystkie światełka
  //   Randomize - generuje losowe ustawienie światełek
  //   (Wygrana może nastąpić tylko po Randomize)
  //   Reset - wyczyszcza plansze (wszystkie światełka OFF)
  //   oraz stan światełek sąsiadujących na przeciwny
  //   Światełka - służą również jako przyciski, po naciśnięciu zmieniają swój stan,
  //   Lights Out Game
endmodule

module button_setup_threes (
  input  pA,
  input  pB,
  input  pD,
  input  pE,
  input  pF,
  input  pJ,
  input  pP,
  input  pT,
  input  pU,
  input  pW,
  input  pY,
  input  pZ,
  input  cA,
  input  cE,
  input  cU,
  input  cZ,
  input  rst,
  input  random_generator,
  output dA,
  output dE,
  output dU,
  output dZ
);

  wire and_1_out, and_2_out, and_3_out, and_4_out, odd_parity_1_out, odd_parity_2_out, odd_parity_3_out,
       odd_parity_4_out;

  and and_1 (and_1_out, cA, random_generator);
  T_Flip_Flop t_ff_1 (.T(1'b1), .clk(odd_parity_1_out), .Q(dA), .reset(rst), .preset(and_1_out));  // open: Qn
  xor odd_parity_1 (odd_parity_1_out, pA, pB, pF);
  and and_2 (and_2_out, cE, random_generator);
  T_Flip_Flop t_ff_2 (.T(1'b1), .clk(odd_parity_2_out), .Q(dE), .reset(rst), .preset(and_2_out));  // open: Qn
  xor odd_parity_2 (odd_parity_2_out, pD, pE, pJ);
  and and_3 (and_3_out, cU, random_generator);
  T_Flip_Flop t_ff_3 (.T(1'b1), .clk(odd_parity_3_out), .Q(dU), .reset(rst), .preset(and_3_out));  // open: Qn
  xor odd_parity_3 (odd_parity_3_out, pP, pW, pU);
  and and_4 (and_4_out, cZ, random_generator);
  T_Flip_Flop t_ff_4 (.T(1'b1), .clk(odd_parity_4_out), .Q(dZ), .reset(rst), .preset(and_4_out));  // open: Qn
  xor odd_parity_4 (odd_parity_4_out, pT, pY, pZ);

  // Other names for the same wires on the sheet: a = pA; b = pB; d = pD; e = pE; f = pF; j = pJ; p = pP; t = pT;
  //   u = pU; w = pW; y = pY; z = pZ
endmodule

module button_setup_fours (
  input  pA,
  input  pB,
  input  pC,
  input  pD,
  input  pE,
  input  pF,
  input  pG,
  input  pH,
  input  pI,
  input  pJ,
  input  pK,
  input  pL,
  input  pN,
  input  pO,
  input  pP,
  input  pQ,
  input  pR,
  input  pS,
  input  pT,
  input  pU,
  input  pW,
  input  pX,
  input  pY,
  input  pZ,
  input  cB,
  input  cF,
  input  cW,
  input  cJ,
  input  cC,
  input  cK,
  input  cX,
  input  cO,
  input  cD,
  input  cP,
  input  cY,
  input  cT,
  input  rst,
  input  random_generator,
  output dB,
  output dF,
  output dW,
  output dJ,
  output dC,
  output dK,
  output dX,
  output dO,
  output dT,
  output dD,
  output dP,
  output dY
);

  wire and_1_out, and_2_out, and_3_out, and_4_out, and_5_out, and_6_out, and_7_out, and_8_out, and_9_out,
       and_10_out, and_11_out, and_12_out, odd_parity_1_out, odd_parity_2_out, odd_parity_3_out,
       odd_parity_4_out, odd_parity_5_out, odd_parity_6_out, odd_parity_7_out, odd_parity_8_out,
       odd_parity_9_out, odd_parity_10_out, odd_parity_11_out, odd_parity_12_out;

  and and_1 (and_1_out, cB, random_generator);
  xor odd_parity_1 (odd_parity_1_out, pA, pB, pC, pG);
  and and_2 (and_2_out, cC, random_generator);
  T_Flip_Flop t_ff_1 (.T(1'b1), .clk(odd_parity_2_out), .Q(dC), .reset(rst), .preset(and_2_out));  // open: Qn
  xor odd_parity_2 (odd_parity_2_out, pD, pB, pC, pH);
  xor odd_parity_3 (odd_parity_3_out, pD, pE, pC, pI);
  T_Flip_Flop t_ff_2 (.T(1'b1), .clk(odd_parity_1_out), .Q(dB), .reset(rst), .preset(and_1_out));  // open: Qn
  and and_3 (and_3_out, cD, random_generator);
  T_Flip_Flop t_ff_3 (.T(1'b1), .clk(odd_parity_3_out), .Q(dD), .reset(rst), .preset(and_3_out));  // open: Qn
  and and_4 (and_4_out, cF, random_generator);
  xor odd_parity_4 (odd_parity_4_out, pA, pF, pK, pG);
  and and_5 (and_5_out, cK, random_generator);
  and and_6 (and_6_out, cP, random_generator);
  T_Flip_Flop t_ff_4 (.T(1'b1), .clk(odd_parity_4_out), .Q(dF), .reset(rst), .preset(and_4_out));  // open: Qn
  T_Flip_Flop t_ff_5 (.T(1'b1), .clk(odd_parity_5_out), .Q(dK), .reset(rst), .preset(and_5_out));  // open: Qn
  xor odd_parity_5 (odd_parity_5_out, pF, pK, pL, pP);
  T_Flip_Flop t_ff_6 (.T(1'b1), .clk(odd_parity_6_out), .Q(dP), .reset(rst), .preset(and_6_out));  // open: Qn
  xor odd_parity_6 (odd_parity_6_out, pK, pP, pU, pQ);
  and and_7 (and_7_out, cW, random_generator);
  T_Flip_Flop t_ff_7 (.T(1'b1), .clk(odd_parity_7_out), .Q(dW), .reset(rst), .preset(and_7_out));  // open: Qn
  xor odd_parity_7 (odd_parity_7_out, pU, pQ, pW, pX);
  and and_8 (and_8_out, cX, random_generator);
  T_Flip_Flop t_ff_8 (.T(1'b1), .clk(odd_parity_8_out), .Q(dX), .reset(rst), .preset(and_8_out));  // open: Qn
  xor odd_parity_8 (odd_parity_8_out, pW, pR, pX, pY);
  and and_9 (and_9_out, cY, random_generator);
  T_Flip_Flop t_ff_9 (.T(1'b1), .clk(odd_parity_9_out), .Q(dY), .reset(rst), .preset(and_9_out));  // open: Qn
  xor odd_parity_9 (odd_parity_9_out, pS, pX, pY, pZ);
  and and_10 (and_10_out, cJ, random_generator);
  xor odd_parity_10 (odd_parity_10_out, pE, pI, pJ, pO);
  and and_11 (and_11_out, cO, random_generator);
  xor odd_parity_11 (odd_parity_11_out, pJ, pN, pO, pT);
  and and_12 (and_12_out, cT, random_generator);
  xor odd_parity_12 (odd_parity_12_out, pO, pS, pT, pZ);
  T_Flip_Flop t_ff_10 (.T(1'b1), .clk(odd_parity_10_out), .Q(dJ), .reset(rst), .preset(and_10_out));  // open: Qn
  T_Flip_Flop t_ff_11 (.T(1'b1), .clk(odd_parity_11_out), .Q(dO), .reset(rst), .preset(and_11_out));  // open: Qn
  T_Flip_Flop t_ff_12 (.T(1'b1), .clk(odd_parity_12_out), .Q(dT), .reset(rst), .preset(and_12_out));  // open: Qn

  // Other names for the same wires on the sheet: a = pA; b = pB; c = pC; d = pD; e = pE; f = pF; g = pG; h = pH;
  //   i = pI; j = pJ; k = pK; l = pL; n = pN; o = pO; p = pP; q = pQ; r = pR; s = pS; t = pT; u = pU; w = pW; x = pX;
  //   y = pY; z = pZ

  // Notes on the sheet:
  //   Górna Półka
  //   Lewa Półka
  //   Dolna Półka
  //   Prawa Półka
endmodule

module button_setup_fives (
  input  pA,
  input  pB,
  input  pC,
  input  pD,
  input  pE,
  input  pF,
  input  pG,
  input  pH,
  input  pI,
  input  pJ,
  input  pK,
  input  pL,
  input  pN,
  input  pO,
  input  pP,
  input  pQ,
  input  pR,
  input  pS,
  input  pT,
  input  pU,
  input  pW,
  input  pX,
  input  pY,
  input  pZ,
  input  pM,
  input  cG,
  input  cI,
  input  cH,
  input  cN,
  input  cM,
  input  cL,
  input  cR,
  input  cQ,
  input  cS,
  input  rst,
  input  random_generizer,
  output dI,
  output dG,
  output dH,
  output dN,
  output dM,
  output dL,
  output dQ,
  output dR,
  output dS
);

  wire and_1_out, and_2_out, and_3_out, and_4_out, and_5_out, and_6_out, and_7_out, and_8_out, and_9_out,
       odd_parity_1_out, odd_parity_2_out, odd_parity_3_out, odd_parity_4_out, odd_parity_5_out,
       odd_parity_6_out, odd_parity_7_out, odd_parity_8_out, odd_parity_9_out;

  and and_1 (and_1_out, cG, random_generizer);
  xor odd_parity_1 (odd_parity_1_out, pF, pB, pG, pH, pL);
  and and_2 (and_2_out, cL, random_generizer);
  xor odd_parity_2 (odd_parity_2_out, pG, pK, pL, pM, pQ);
  and and_3 (and_3_out, cQ, random_generizer);
  xor odd_parity_3 (odd_parity_3_out, pL, pP, pQ, pR, pW);
  T_Flip_Flop t_ff_1 (.T(1'b1), .clk(odd_parity_1_out), .Q(dG), .reset(rst), .preset(and_1_out));  // open: Qn
  T_Flip_Flop t_ff_2 (.T(1'b1), .clk(odd_parity_2_out), .Q(dL), .reset(rst), .preset(and_2_out));  // open: Qn
  T_Flip_Flop t_ff_3 (.T(1'b1), .clk(odd_parity_3_out), .Q(dQ), .reset(rst), .preset(and_3_out));  // open: Qn
  and and_4 (and_4_out, cH, random_generizer);
  T_Flip_Flop t_ff_4 (.T(1'b1), .clk(odd_parity_4_out), .Q(dH), .reset(rst), .preset(and_4_out));  // open: Qn
  xor odd_parity_4 (odd_parity_4_out, pC, pG, pH, pI, pM);
  and and_5 (and_5_out, cM, random_generizer);
  T_Flip_Flop t_ff_5 (.T(1'b1), .clk(odd_parity_5_out), .Q(dM), .reset(rst), .preset(and_5_out));  // open: Qn
  xor odd_parity_5 (odd_parity_5_out, pH, pL, pM, pN, pR);
  and and_6 (and_6_out, cR, random_generizer);
  T_Flip_Flop t_ff_6 (.T(1'b1), .clk(odd_parity_6_out), .Q(dR), .reset(rst), .preset(and_6_out));  // open: Qn
  xor odd_parity_6 (odd_parity_6_out, pM, pQ, pR, pS, pX);
  and and_7 (and_7_out, cI, random_generizer);
  xor odd_parity_7 (odd_parity_7_out, pD, pH, pI, pJ, pN);
  and and_8 (and_8_out, cN, random_generizer);
  xor odd_parity_8 (odd_parity_8_out, pI, pM, pN, pO, pS);
  and and_9 (and_9_out, cS, random_generizer);
  T_Flip_Flop t_ff_7 (.T(1'b1), .clk(odd_parity_9_out), .Q(dS), .reset(rst), .preset(and_9_out));  // open: Qn
  xor odd_parity_9 (odd_parity_9_out, pN, pR, pS, pT, pY);
  T_Flip_Flop t_ff_8 (.T(1'b1), .clk(odd_parity_7_out), .Q(dI), .reset(rst), .preset(and_7_out));  // open: Qn
  T_Flip_Flop t_ff_9 (.T(1'b1), .clk(odd_parity_8_out), .Q(dN), .reset(rst), .preset(and_8_out));  // open: Qn

  // Other names for the same wires on the sheet: a = pA; b = pB; c = pC; d = pD; e = pE; f = pF; g = pG; h = pH;
  //   i = pI; j = pJ; k = pK; l = pL; m = pM; n = pN; o = pO; p = pP; q = pQ; r = pR; s = pS; t = pT; u = pU; w = pW;
  //   x = pX; y = pY; z = pZ
endmodule

module wincon (
  input  pA,
  input  pB,
  input  pC,
  input  pD,
  input  pE,
  input  pF,
  input  pG,
  input  pH,
  input  pI,
  input  pJ,
  input  pK,
  input  pL,
  input  pN,
  input  pO,
  input  pP,
  input  pQ,
  input  pR,
  input  pS,
  input  pT,
  input  pU,
  input  pW,
  input  pX,
  input  pY,
  input  pZ,
  input  pM,
  input  random,
  input  reset,
  output WIN
);

  wire not_1_out, not_2_out, not_3_out, not_4_out, not_5_out, not_6_out, not_7_out, not_8_out, not_9_out,
       not_10_out, not_11_out, not_12_out, not_13_out, not_14_out, not_15_out, not_16_out, not_17_out,
       not_18_out, not_19_out, not_20_out, not_21_out, not_22_out, not_23_out, not_24_out, not_25_out,
       t_ff_1_q;

  T_Flip_Flop t_ff_1 (.T(1'b1), .Q(t_ff_1_q), .reset(reset), .preset(random));  // open: clk, Qn
  not not_1 (not_1_out, pA);
  not not_2 (not_2_out, pC);
  not not_3 (not_3_out, pE);
  not not_4 (not_4_out, pG);
  not not_5 (not_5_out, pI);
  not not_6 (not_6_out, pK);
  not not_7 (not_7_out, pN);
  not not_8 (not_8_out, pP);
  not not_9 (not_9_out, pR);
  not not_10 (not_10_out, pT);
  not not_11 (not_11_out, pW);
  not not_12 (not_12_out, pY);
  not not_13 (not_13_out, pM);
  not not_14 (not_14_out, pB);
  not not_15 (not_15_out, pD);
  not not_16 (not_16_out, pF);
  not not_17 (not_17_out, pH);
  not not_18 (not_18_out, pJ);
  not not_19 (not_19_out, pL);
  not not_20 (not_20_out, pO);
  not not_21 (not_21_out, pQ);
  not not_22 (not_22_out, pS);
  not not_23 (not_23_out, pU);
  not not_24 (not_24_out, pX);
  not not_25 (not_25_out, pZ);
  and and_1 (WIN, not_1_out, not_14_out, not_2_out, not_15_out, not_3_out, not_16_out, not_4_out, not_17_out, not_5_out, not_18_out, not_6_out, not_19_out, not_20_out, not_8_out, not_21_out, not_9_out, not_22_out, not_10_out, not_23_out, not_11_out, not_24_out, not_12_out, not_25_out, not_13_out, t_ff_1_q);
endmodule

module randomizer (
  input  random_gen,
  output a,
  output b,
  output c,
  output d,
  output e,
  output f,
  output g,
  output h,
  output i,
  output j,
  output k,
  output l,
  output m,
  output n,
  output o,
  output p,
  output q,
  output r,
  output s,
  output t,
  output u,
  output w,
  output x,
  output y,
  output z
);

  Random #(.width(25)) random_1 (
    .clk(random_gen), .out({z, y, x, w, u, t, s, r, q, p, o, n, m, l, k, j, i, h, g, f, e, d, c, b, a}));  // open: clr, next
endmodule
